# Fritzing sketch no.code.rgb.controller (saved by Fritzing 0.9.3b)
breadboards: 1

parts:
  S1 = Pushbutton [package="[THT]"]
  S2 = Pushbutton [package="[THT]"]
  S3 = Pushbutton [package="[THT]"]
  LED1 = RGB LED (com. cathode, rgb) [package="5 mm [THT]"]
  R1 = Resistor [tolerance=±5% resistance=330 package=THT]
  Part1 = Arduino Uno (Rev3)

nets:
  N1: S1.Pin_1, S1.Pin_2, S2.Pin_1, S2.Pin_2, S3.Pin_1, S3.Pin_2, Part1.3V3
  N2: S1.Pin_3, S1.Pin_4, LED1.green_anode
  N3: S2.Pin_3, S2.Pin_4, LED1.red_anode
  N4: S3.Pin_3, S3.Pin_4, LED1.blue_anode
  N5: LED1.common_cathode, R1.Pin_1, Part1.GND
